# Fritzing sketch MKRZero (saved by Fritzing 0.9.9b)
breadboards: 1

parts:
  M1 = MKR ZERO
  B4 = Pushbutton [package=THT]
  B3 = Pushbutton [package=THT]
  B2 = Pushbutton [package=THT]
  B1 = Pushbutton [package=THT]
  B5 = Pushbutton [package=THT]
  B5_2 = Pushbutton [package=THT]
  R1 = Resistor [tolerance=±5% power=0.25 resistance=1k package=THT]
  R2 = Resistor [tolerance=±5% power=0.25 resistance=1k package=THT]
  R3 = Resistor [tolerance=±5% power=0.25 resistance=1k package=THT]
  R4 = Resistor [tolerance=±5% power=0.25 resistance=1k package=THT]
  R5 = Resistor [tolerance=±5% power=0.25 resistance=1k package=THT]
  R6 = Resistor [tolerance=±5% power=0.25 resistance=1k package=THT]
  Part1 = Adafruit MAX98357A I2S 3W Class D Amplifier [part_number="Adafruit #3006"]
  R7 = Resistor [tolerance=±5% power=0.25 resistance=100k package=THT]
  R8 = Resistor [tolerance=±5% power=0.25 resistance=330 package=THT]
  LED1 = LED - 5mm [color="Green (565nm)" current=0.030 package="5 mm [THT]"]

nets:
  N1: M1.A6, Part1.DIN
  N2: M1.D0, B1.leg0, R1.Pin_0
  N3: M1.D1, B2.leg0, R2.Pin_0
  N4: M1.D2_PWM, Part1.LRCLK
  N5: M1.D3_PWM, Part1.BCLK
  N6: M1.D4_PWM, B3.leg0, R3.Pin_0
  N7: M1.D5_PWM, B4.leg0, R4.Pin_0
  N8: M1.D6, B5.leg0, R5.Pin_0
  N9: M1.D7, B5_2.leg0, R6.Pin_0
  GND: M1.GND, M1.-VBAT, R1.Pin_1, R2.Pin_1, R3.Pin_1, R4.Pin_1, R5.Pin_1, R6.Pin_1, Part1.GND, R7.Pin_1, LED1.cathode
  N10: M1.VCC, B4.leg1, B3.leg1, B2.leg1, B1.leg1, B5.leg1, B5_2.leg1, R8.Pin_0
  5V: M1.5V, M1.+5V, Part1.VIN
  N11: Part1.GAIN, R7.Pin_0
  N12: R8.Pin_1, LED1.anode

custom parts:
  MKR ZERO: arduino mrk zero SAMD21 Cortex-M0+ 32bit low power ARM MCU 256 meg flash 32kb sram 48mhz
  Adafruit MAX98357A I2S 3W Class D Amplifier: Listen to this good news - we now have an all in one digital audio amp breakout board that works incredibly well with the Raspberry Pi! If you're looking for an easy and low cost way to get you digital sound files bumpin' then the MAX08357 I2S Amp Breakout is for you. It takes standard I2S digital audio input and, not only decodes it into analog, but also amplifies it directly into a speaker.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
